// Logisim project Trabalho.circ as structural Verilog: 16 circuits, main circuit main
module main (
);


  // Notes on the sheet:
  //   e depois use aquele circuito para construir sua calculadora.
  //   Este projeto foi fornecido apenas para que você altere o circuito alu-8-bits,
endmodule

module alu_8_bits (
  input  [7:0] A,
  input  [7:0] B,
  input  [2:0] OP,
  input  Cin,
  output c,
  output z,
  output [7:0] s
);

  wire or_2_out, shift_left_8_bits_1_cout, somador_8_bits_1_qout, subtracao_8_bits_1_qout;
  wire [7:0] and_8_bits_1_s, dmux_1p8_8bit_1_s1, dmux_1p8_8bit_1_s2, dmux_1p8_8bit_1_s3, dmux_1p8_8bit_1_s4,
       dmux_1p8_8bit_1_s5, dmux_1p8_8bit_1_s6, dmux_1p8_8bit_1_s7, dmux_1p8_8bit_1_s8, dmux_1p8_8bit_2_s1,
       dmux_1p8_8bit_2_s2, dmux_1p8_8bit_2_s3, dmux_1p8_8bit_2_s4, dmux_1p8_8bit_2_s5, dmux_1p8_8bit_2_s6,
       or_8_bits_1_s, or_8_bits_2_s, shift_left_8_bits_1_s, shift_right_8_bits_1_s, somador_8_bits_1_s,
       subtracao_8_bits_1_s, xor_8_bits_1_s;

  or or_1 (c, or_2_out, shift_left_8_bits_1_cout);
  or or_2 (or_2_out, somador_8_bits_1_qout, subtracao_8_bits_1_qout);
  DMUX_1p8_8bit dmux_1p8_8bit_1 (
    .MUX(OP), .S8(dmux_1p8_8bit_1_s8), .S7(dmux_1p8_8bit_1_s7), .S6(dmux_1p8_8bit_1_s6),
    .S5(dmux_1p8_8bit_1_s5), .S4(dmux_1p8_8bit_1_s4), .S3(dmux_1p8_8bit_1_s3), .S2(dmux_1p8_8bit_1_s2),
    .S1(dmux_1p8_8bit_1_s1), .A(A));
  DMUX_1p8_8bit dmux_1p8_8bit_2 (
    .MUX(OP), .S6(dmux_1p8_8bit_2_s6), .S5(dmux_1p8_8bit_2_s5), .S4(dmux_1p8_8bit_2_s4),
    .S3(dmux_1p8_8bit_2_s3), .S2(dmux_1p8_8bit_2_s2), .S1(dmux_1p8_8bit_2_s1), .A(B));  // open: S8, S7
  somador_8_bits somador_8_bits_1 (
    .S(somador_8_bits_1_s), .Qout(somador_8_bits_1_qout), .A(dmux_1p8_8bit_1_s1), .B(dmux_1p8_8bit_2_s1),
    .in_1(Cin));
  Subtracao_8_bits subtracao_8_bits_1 (
    .S(subtracao_8_bits_1_s), .Qout(subtracao_8_bits_1_qout), .A(dmux_1p8_8bit_1_s2), .B(dmux_1p8_8bit_2_s2));
  XOR_8_bits xor_8_bits_1 (.S(xor_8_bits_1_s), .A(dmux_1p8_8bit_1_s3), .B(dmux_1p8_8bit_2_s3));
  AND_8_bits and_8_bits_1 (.S(and_8_bits_1_s), .A(dmux_1p8_8bit_1_s5), .B(dmux_1p8_8bit_2_s5));
  OR_8_bits or_8_bits_1 (.S(or_8_bits_1_s), .A(dmux_1p8_8bit_1_s4), .B(dmux_1p8_8bit_2_s4));
  OR_8_bits_7x or_8_bits_7x_1 (
    .in_7(somador_8_bits_1_s), .in_6(subtracao_8_bits_1_s), .in_5(xor_8_bits_1_s), .in_4(or_8_bits_1_s),
    .in_3(and_8_bits_1_s), .in_2(shift_left_8_bits_1_s), .in_1(shift_right_8_bits_1_s), .out_8(s));
  Shift_Left_8_bits shift_left_8_bits_1 (
    .B(dmux_1p8_8bit_1_s6), .S(shift_left_8_bits_1_s), .Cout(shift_left_8_bits_1_cout));
  Shift_Right_8_bits shift_right_8_bits_1 (.B(dmux_1p8_8bit_1_s7), .S(shift_right_8_bits_1_s), .Cin(Cin));
  OR_8_bits or_8_bits_2 (.S(or_8_bits_2_s), .A(s), .B({8{1'b0}}));
  Igual_0_8b igual_0_8b_1 (.out_2(z), .in_1(or_8_bits_2_s));
endmodule

module somador_2_bits (
  input  A,
  input  B,
  input  Qin,
  output S,
  output Qout
);

  wire and_1_out, and_2_out, and_3_out, and_4_out, and_5_out, and_6_out, and_7_out, not_1_out, not_2_out,
       not_3_out, not_4_out, not_5_out, not_6_out;

  not not_1 (not_1_out, A);
  not not_2 (not_2_out, B);
  not not_3 (not_3_out, A);
  not not_4 (not_4_out, Qin);
  not not_5 (not_5_out, B);
  not not_6 (not_6_out, Qin);
  and and_1 (and_1_out, B, Qin);
  and and_2 (and_2_out, A, Qin);
  and and_3 (and_3_out, A, B);
  and and_4 (and_4_out, not_1_out, not_2_out, Qin);
  and and_5 (and_5_out, not_3_out, B, not_4_out);
  and and_6 (and_6_out, A, not_5_out, not_6_out);
  and and_7 (and_7_out, A, B, Qin);
  or or_1 (Qout, and_1_out, and_2_out, and_3_out);
  or or_2 (S, and_4_out, and_5_out, and_6_out, and_7_out);
endmodule

module somador_8_bits (
  input  in_1,
  input  [7:0] A,
  input  [7:0] B,
  output [7:0] S,
  output Qout
);

  wire somador_2_bits_2_qout, somador_2_bits_3_qout, somador_2_bits_4_qout, somador_2_bits_5_qout,
       somador_2_bits_6_qout, somador_2_bits_7_qout, somador_2_bits_8_qout;

  somador_2_bits somador_2_bits_1 (.A(A[7]), .B(B[7]), .Qin(somador_2_bits_2_qout), .S(S[7]), .Qout(Qout));
  somador_2_bits somador_2_bits_2 (
    .A(A[6]), .B(B[6]), .Qin(somador_2_bits_3_qout), .S(S[6]), .Qout(somador_2_bits_2_qout));
  somador_2_bits somador_2_bits_3 (
    .A(A[5]), .B(B[5]), .Qin(somador_2_bits_4_qout), .S(S[5]), .Qout(somador_2_bits_3_qout));
  somador_2_bits somador_2_bits_4 (
    .A(A[4]), .B(B[4]), .Qin(somador_2_bits_5_qout), .S(S[4]), .Qout(somador_2_bits_4_qout));
  somador_2_bits somador_2_bits_5 (
    .A(A[3]), .B(B[3]), .Qin(somador_2_bits_6_qout), .S(S[3]), .Qout(somador_2_bits_5_qout));
  somador_2_bits somador_2_bits_6 (
    .A(A[2]), .B(B[2]), .Qin(somador_2_bits_7_qout), .S(S[2]), .Qout(somador_2_bits_6_qout));
  somador_2_bits somador_2_bits_7 (
    .A(A[1]), .B(B[1]), .Qin(somador_2_bits_8_qout), .S(S[1]), .Qout(somador_2_bits_7_qout));
  somador_2_bits somador_2_bits_8 (.A(A[0]), .B(B[0]), .Qin(in_1), .S(S[0]), .Qout(somador_2_bits_8_qout));
endmodule

module XOR_2_bits (
  input  A,
  input  B,
  output S
);

  wire and_1_out, and_2_out, not_1_out, not_2_out;

  not not_1 (not_1_out, A);
  not not_2 (not_2_out, B);
  and and_1 (and_1_out, not_1_out, B);
  and and_2 (and_2_out, A, not_2_out);
  or or_1 (S, and_1_out, and_2_out);
endmodule

module XOR_8_bits (
  input  [7:0] A,
  input  [7:0] B,
  output [7:0] S
);

  XOR_2_bits xor_2_bits_1 (.A(A[7]), .B(B[7]), .S(S[7]));
  XOR_2_bits xor_2_bits_2 (.A(A[6]), .B(B[6]), .S(S[6]));
  XOR_2_bits xor_2_bits_3 (.A(A[5]), .B(B[5]), .S(S[5]));
  XOR_2_bits xor_2_bits_4 (.A(A[3]), .B(B[3]), .S(S[3]));
  XOR_2_bits xor_2_bits_5 (.A(A[4]), .B(B[4]), .S(S[4]));
  XOR_2_bits xor_2_bits_6 (.A(A[2]), .B(B[2]), .S(S[2]));
  XOR_2_bits xor_2_bits_7 (.A(A[1]), .B(B[1]), .S(S[1]));
  XOR_2_bits xor_2_bits_8 (.A(A[0]), .B(B[0]), .S(S[0]));
endmodule

module AND_8_bits (
  input  [7:0] A,
  input  [7:0] B,
  output [7:0] S
);

  and and_1 (S[7], A[7], B[7]);
  and and_2 (S[6], A[6], B[6]);
  and and_3 (S[5], A[5], B[5]);
  and and_4 (S[4], A[4], B[4]);
  and and_5 (S[3], A[3], B[3]);
  and and_6 (S[2], A[2], B[2]);
  and and_7 (S[1], A[1], B[1]);
  and and_8 (S[0], A[0], B[0]);
endmodule

module OR_8_bits (
  input  [7:0] A,
  input  [7:0] B,
  output [7:0] S
);

  or or_1 (S[7], A[7], B[7]);
  or or_2 (S[6], A[6], B[6]);
  or or_3 (S[5], A[5], B[5]);
  or or_4 (S[4], A[4], B[4]);
  or or_5 (S[3], A[3], B[3]);
  or or_6 (S[2], A[2], B[2]);
  or or_7 (S[1], A[1], B[1]);
  or or_8 (S[0], A[0], B[0]);
endmodule

module Shift_Left_8_bits (
  input  [7:0] B,
  output [7:0] S,
  output Cout
);


  assign Cout = B[7];
  assign S = {B[6:0], 1'b0};
endmodule

module Shift_Right_8_bits (
  input  [7:0] B,
  input  Cin,
  output [7:0] S
);


  assign S = {Cin, B[7:1]};
endmodule

module Subtracao_8_bits (
  input  [7:0] A,
  input  [7:0] B,
  output [7:0] S,
  output Qout
);

  wire not_2_out, not_3_out, not_4_out, not_5_out, not_6_out, not_7_out, not_8_out, not_9_out,
       somador_2_bits_1_qout, somador_2_bits_2_qout, somador_2_bits_3_qout, somador_2_bits_4_qout,
       somador_2_bits_5_qout, somador_2_bits_6_qout, somador_2_bits_7_qout, somador_2_bits_8_qout;

  not not_1 (Qout, somador_2_bits_1_qout);
  not not_2 (not_2_out, B[7]);
  not not_3 (not_3_out, B[6]);
  not not_4 (not_4_out, B[5]);
  not not_5 (not_5_out, B[4]);
  not not_6 (not_6_out, B[3]);
  not not_7 (not_7_out, B[2]);
  not not_8 (not_8_out, B[1]);
  not not_9 (not_9_out, B[0]);
  somador_2_bits somador_2_bits_1 (
    .A(A[7]), .B(not_2_out), .Qin(somador_2_bits_2_qout), .S(S[7]), .Qout(somador_2_bits_1_qout));
  somador_2_bits somador_2_bits_2 (
    .A(A[6]), .B(not_3_out), .Qin(somador_2_bits_3_qout), .S(S[6]), .Qout(somador_2_bits_2_qout));
  somador_2_bits somador_2_bits_3 (
    .A(A[5]), .B(not_4_out), .Qin(somador_2_bits_4_qout), .S(S[5]), .Qout(somador_2_bits_3_qout));
  somador_2_bits somador_2_bits_4 (
    .A(A[4]), .B(not_5_out), .Qin(somador_2_bits_5_qout), .S(S[4]), .Qout(somador_2_bits_4_qout));
  somador_2_bits somador_2_bits_5 (
    .A(A[3]), .B(not_6_out), .Qin(somador_2_bits_6_qout), .S(S[3]), .Qout(somador_2_bits_5_qout));
  somador_2_bits somador_2_bits_6 (
    .A(A[2]), .B(not_7_out), .Qin(somador_2_bits_7_qout), .S(S[2]), .Qout(somador_2_bits_6_qout));
  somador_2_bits somador_2_bits_7 (
    .A(A[1]), .B(not_8_out), .Qin(somador_2_bits_8_qout), .S(S[1]), .Qout(somador_2_bits_7_qout));
  somador_2_bits somador_2_bits_8 (.A(A[0]), .B(not_9_out), .Qin(1'b1), .S(S[0]), .Qout(somador_2_bits_8_qout));
endmodule

module DMUX_1p2_1bit (
  input  A,
  input  Op,
  output S1,
  output S2
);

  wire not_1_out;

  not not_1 (not_1_out, Op);
  and and_1 (S2, A, Op);
  and and_2 (S1, A, not_1_out);
endmodule

module DMUX_1p2_8bit (
  input  MUX,
  input  [7:0] A,
  output [7:0] S1,
  output [7:0] S2
);

  DMUX_1p2_1bit dmux_1p2_1bit_1 (.A(A[6]), .Op(MUX), .S1(S1[6]), .S2(S2[6]));
  DMUX_1p2_1bit dmux_1p2_1bit_2 (.A(A[7]), .Op(MUX), .S1(S1[7]), .S2(S2[7]));
  DMUX_1p2_1bit dmux_1p2_1bit_3 (.A(A[5]), .Op(MUX), .S1(S1[5]), .S2(S2[5]));
  DMUX_1p2_1bit dmux_1p2_1bit_4 (.A(A[3]), .Op(MUX), .S1(S1[3]), .S2(S2[3]));
  DMUX_1p2_1bit dmux_1p2_1bit_5 (.A(A[4]), .Op(MUX), .S1(S1[4]), .S2(S2[4]));
  DMUX_1p2_1bit dmux_1p2_1bit_6 (.A(A[1]), .Op(MUX), .S1(S1[1]), .S2(S2[1]));
  DMUX_1p2_1bit dmux_1p2_1bit_7 (.A(A[2]), .Op(MUX), .S1(S1[2]), .S2(S2[2]));
  DMUX_1p2_1bit dmux_1p2_1bit_8 (.A(A[0]), .Op(MUX), .S1(S1[0]), .S2(S2[0]));
endmodule

module DMUX_1p8_8bit (
  input  [2:0] MUX,
  input  [7:0] A,
  output [7:0] S8,
  output [7:0] S6,
  output [7:0] S4,
  output [7:0] S2,
  output [7:0] S7,
  output [7:0] S5,
  output [7:0] S3,
  output [7:0] S1
);

  wire [7:0] dmux_1p2_8bit_3_s1, dmux_1p2_8bit_3_s2, dmux_1p2_8bit_4_s1, dmux_1p2_8bit_4_s2,
       dmux_1p2_8bit_7_s1, dmux_1p2_8bit_7_s2;

  DMUX_1p2_8bit dmux_1p2_8bit_1 (.S1(S7), .MUX(MUX[0]), .S2(S8), .A(dmux_1p2_8bit_3_s2));
  DMUX_1p2_8bit dmux_1p2_8bit_2 (.S1(S5), .MUX(MUX[0]), .S2(S6), .A(dmux_1p2_8bit_3_s1));
  DMUX_1p2_8bit dmux_1p2_8bit_3 (
    .S1(dmux_1p2_8bit_3_s1), .MUX(MUX[1]), .S2(dmux_1p2_8bit_3_s2), .A(dmux_1p2_8bit_4_s2));
  DMUX_1p2_8bit dmux_1p2_8bit_4 (.S1(dmux_1p2_8bit_4_s1), .MUX(MUX[2]), .S2(dmux_1p2_8bit_4_s2), .A(A));
  DMUX_1p2_8bit dmux_1p2_8bit_5 (.S1(S1), .MUX(MUX[0]), .S2(S2), .A(dmux_1p2_8bit_7_s1));
  DMUX_1p2_8bit dmux_1p2_8bit_6 (.S1(S3), .MUX(MUX[0]), .S2(S4), .A(dmux_1p2_8bit_7_s2));
  DMUX_1p2_8bit dmux_1p2_8bit_7 (
    .S1(dmux_1p2_8bit_7_s1), .MUX(MUX[1]), .S2(dmux_1p2_8bit_7_s2), .A(dmux_1p2_8bit_4_s1));
endmodule

module OR_8_bits_7x (
  input  [7:0] in_1,
  input  [7:0] in_2,
  input  [7:0] in_3,
  input  [7:0] in_4,
  input  [7:0] in_5,
  input  [7:0] in_6,
  input  [7:0] in_7,
  output [7:0] out_8
);

  wire [7:0] or_8_bits_1_s, or_8_bits_2_s, or_8_bits_3_s, or_8_bits_5_s, or_8_bits_6_s;

  OR_8_bits or_8_bits_1 (.S(or_8_bits_1_s), .A(or_8_bits_2_s), .B(or_8_bits_3_s));
  OR_8_bits or_8_bits_2 (.S(or_8_bits_2_s), .A(in_1), .B(in_5));
  OR_8_bits or_8_bits_3 (.S(or_8_bits_3_s), .A(in_2), .B(in_6));
  OR_8_bits or_8_bits_4 (.S(out_8), .A(or_8_bits_1_s), .B(or_8_bits_5_s));
  OR_8_bits or_8_bits_5 (.S(or_8_bits_5_s), .A(or_8_bits_6_s), .B(in_4));
  OR_8_bits or_8_bits_6 (.S(or_8_bits_6_s), .A(in_3), .B(in_7));
endmodule

module Igual_0_8b (
  input  [7:0] in_1,
  output out_2
);

  wire or_1_out, or_2_out, or_3_out, or_4_out, or_5_out, or_6_out, or_7_out;

  or or_1 (or_1_out, or_2_out, or_3_out);
  or or_2 (or_2_out, in_1[7], in_1[6]);
  or or_3 (or_3_out, in_1[5], in_1[4]);
  not not_1 (out_2, or_4_out);
  or or_4 (or_4_out, or_1_out, or_5_out);
  or or_5 (or_5_out, or_6_out, or_7_out);
  or or_6 (or_6_out, in_1[3], in_1[2]);
  or or_7 (or_7_out, in_1[1], in_1[0]);
endmodule
