// Logisim project renan_trabalho.circ as structural Verilog: 11 circuits, main circuit main
module ADD (
  input  a,
  input  b,
  input  cin,
  output cout,
  output s
);

  wire and_1_out, and_2_out, and_3_out, and_4_out, and_5_out, and_6_out, and_7_out, not_1_out, not_2_out,
       not_3_out, not_4_out, not_5_out, not_6_out;

  and and_1 (and_1_out, b, cin);
  and and_2 (and_2_out, a, cin);
  and and_3 (and_3_out, a, b);
  not not_1 (not_1_out, a);
  not not_2 (not_2_out, b);
  not not_3 (not_3_out, a);
  not not_4 (not_4_out, cin);
  not not_5 (not_5_out, b);
  not not_6 (not_6_out, cin);
  or or_1 (cout, and_1_out, and_2_out, and_3_out);
  and and_4 (and_4_out, not_1_out, not_2_out, cin);
  and and_5 (and_5_out, not_3_out, b, not_4_out);
  and and_6 (and_6_out, a, not_5_out, not_6_out);
  and and_7 (and_7_out, a, b, cin);
  or or_2 (s, and_4_out, and_5_out, and_6_out, and_7_out);
endmodule

module main (
  input  [7:0] in_1,
  input  [7:0] in_2,
  input  in_3,
  input  in_4,
  input  in_5,
  input  in_6,
  output out_7
);

  wire decodificador_16_1_a, decodificador_16_1_b, decodificador_16_1_c, decodificador_16_1_d,
       decodificador_16_1_e, decodificador_16_1_f, decodificador_16_1_g;
  wire [6:0] n2_dec_16_1_out_2, n2_dec_16_1_out_3;
  wire [7:0] add_8_1_out_4;

  ADD_8 add_8_1 (.in_3(out_7), .in_1(in_2), .in_2(in_1), .out_4(add_8_1_out_4));
  DECODIFICADOR_16 decodificador_16_1 (
    .a0(in_3), .a1(in_4), .a2(in_5), .a3(in_6), .a(decodificador_16_1_a), .b(decodificador_16_1_b),
    .c(decodificador_16_1_c), .d(decodificador_16_1_d), .e(decodificador_16_1_e), .f(decodificador_16_1_f),
    .g(decodificador_16_1_g));
  _7_Segment_Display u_7_segment_display_1 (
    .g(decodificador_16_1_g), .f(decodificador_16_1_f), .a(decodificador_16_1_a), .b(decodificador_16_1_b),
    .e(decodificador_16_1_e), .d(decodificador_16_1_d), .c(decodificador_16_1_c));  // open: dp
  _2_DEC_16 u_2_dec_16_1 (.in_1(add_8_1_out_4), .out_2(n2_dec_16_1_out_2), .out_3(n2_dec_16_1_out_3));
  _7_Segment_Display u_7_segment_display_2 (
    .g(n2_dec_16_1_out_2[6]), .f(n2_dec_16_1_out_2[5]), .a(n2_dec_16_1_out_2[0]), .b(n2_dec_16_1_out_2[1]),
    .e(n2_dec_16_1_out_2[4]), .d(n2_dec_16_1_out_2[3]), .c(n2_dec_16_1_out_2[2]));  // open: dp
  _7_Segment_Display u_7_segment_display_3 (
    .g(n2_dec_16_1_out_3[6]), .f(n2_dec_16_1_out_3[5]), .a(n2_dec_16_1_out_3[0]), .b(n2_dec_16_1_out_3[1]),
    .e(n2_dec_16_1_out_3[4]), .d(n2_dec_16_1_out_3[3]), .c(n2_dec_16_1_out_3[2]));  // open: dp
endmodule

module ADD_8 (
  input  [7:0] in_1,
  input  [7:0] in_2,
  input  in_3,
  output [7:0] out_4
);

  wire add_1_cout, add_2_cout, add_3_cout, add_4_cout, add_5_cout, add_6_cout, add_7_cout;

  ADD add_1 (.a(in_2[0]), .b(in_1[0]), .cin(1'b0), .cout(add_1_cout), .s(out_4[0]));
  ADD add_2 (.a(in_2[1]), .b(in_1[1]), .cin(add_1_cout), .cout(add_2_cout), .s(out_4[1]));
  ADD add_3 (.a(in_2[2]), .b(in_1[2]), .cin(add_2_cout), .cout(add_3_cout), .s(out_4[2]));
  ADD add_4 (.a(in_2[3]), .b(in_1[3]), .cin(add_3_cout), .cout(add_4_cout), .s(out_4[3]));
  ADD add_5 (.a(in_2[4]), .b(in_1[4]), .cin(add_4_cout), .cout(add_5_cout), .s(out_4[4]));
  ADD add_6 (.a(in_2[5]), .b(in_1[5]), .cin(add_5_cout), .cout(add_6_cout), .s(out_4[5]));
  ADD add_7 (.a(in_2[6]), .b(in_1[6]), .cin(add_6_cout), .cout(add_7_cout), .s(out_4[6]));
  ADD add_8 (.a(in_2[7]), .b(in_1[7]), .cin(add_7_cout), .cout(in_3), .s(out_4[7]));
endmodule

module XOR (
  input  a,
  input  b,
  output s
);

  wire and_1_out, and_2_out, not_1_out, not_2_out;

  not not_1 (not_1_out, a);
  not not_2 (not_2_out, b);
  and and_1 (and_1_out, not_1_out, b);
  and and_2 (and_2_out, a, not_2_out);
  or or_1 (s, and_1_out, and_2_out);
endmodule

module XOR_8 (
  input  [7:0] in_1,
  input  [7:0] in_2,
  output [7:0] out_3
);

  XOR xor_1 (.a(in_2[0]), .b(in_1[0]), .s(out_3[0]));
  XOR xor_2 (.a(in_2[1]), .b(in_1[1]), .s(out_3[1]));
  XOR xor_3 (.a(in_2[2]), .b(in_1[2]), .s(out_3[2]));
  XOR xor_4 (.a(in_2[3]), .b(in_1[3]), .s(out_3[3]));
  XOR xor_5 (.a(in_2[4]), .b(in_1[4]), .s(out_3[4]));
  XOR xor_6 (.a(in_2[5]), .b(in_1[5]), .s(out_3[5]));
  XOR xor_7 (.a(in_2[6]), .b(in_1[6]), .s(out_3[6]));
  XOR xor_8 (.a(in_2[7]), .b(in_1[7]), .s(out_3[7]));
endmodule

module OR (
  input  a,
  input  b,
  output s
);

  or or_1 (s, b, a);
endmodule

module OR_8 (
  input  [7:0] in_1,
  input  [7:0] in_2,
  output [7:0] out_3
);

  OR or_1 (.a(in_2[0]), .b(in_1[0]), .s(out_3[0]));
  OR or_2 (.a(in_2[1]), .b(in_1[1]), .s(out_3[1]));
  OR or_3 (.a(in_2[2]), .b(in_1[2]), .s(out_3[2]));
  OR or_4 (.a(in_2[3]), .b(in_1[3]), .s(out_3[3]));
  OR or_5 (.a(in_2[4]), .b(in_1[4]), .s(out_3[4]));
  OR or_6 (.a(in_2[5]), .b(in_1[5]), .s(out_3[5]));
  OR or_7 (.a(in_2[6]), .b(in_1[6]), .s(out_3[6]));
  OR or_8 (.a(in_2[7]), .b(in_1[7]), .s(out_3[7]));
endmodule

module AND (
  input  a,
  input  b,
  output s
);

  and and_1 (s, a, b);
endmodule

module AND_8 (
  input  [7:0] in_1,
  input  [7:0] in_2,
  output [7:0] out_3
);

  AND and_1 (.a(in_2[0]), .b(in_1[0]), .s(out_3[0]));
  AND and_2 (.a(in_2[1]), .b(in_1[1]), .s(out_3[1]));
  AND and_3 (.a(in_2[2]), .b(in_1[2]), .s(out_3[2]));
  AND and_4 (.a(in_2[3]), .b(in_1[3]), .s(out_3[3]));
  AND and_5 (.a(in_2[4]), .b(in_1[4]), .s(out_3[4]));
  AND and_6 (.a(in_2[5]), .b(in_1[5]), .s(out_3[5]));
  AND and_7 (.a(in_2[6]), .b(in_1[6]), .s(out_3[6]));
  AND and_8 (.a(in_2[7]), .b(in_1[7]), .s(out_3[7]));
endmodule

module DECODIFICADOR_16 (
  input  a0,
  input  a1,
  input  a2,
  input  a3,
  output a,
  output b,
  output c,
  output d,
  output e,
  output f,
  output g
);

  wire and_1_out, and_2_out, and_3_out, and_4_out, and_5_out, and_6_out, and_7_out, and_8_out, and_9_out,
       and_10_out, and_11_out, and_12_out, and_13_out, and_14_out, and_15_out, and_16_out, and_17_out,
       and_18_out, and_19_out, and_20_out, and_21_out, and_22_out, and_23_out, and_24_out, and_25_out,
       and_26_out, and_27_out, and_28_out, and_29_out, and_30_out, and_31_out, and_32_out, and_33_out,
       and_34_out, and_35_out, not_1_out, not_2_out, not_3_out, not_4_out, not_5_out, not_6_out, not_7_out,
       not_8_out, not_9_out, not_10_out, not_11_out, not_12_out, not_13_out, not_14_out, not_15_out,
       not_16_out, not_17_out, not_18_out, not_19_out, not_20_out, not_21_out, not_22_out, not_23_out,
       not_24_out, not_25_out, not_26_out, not_27_out, not_28_out, not_29_out, not_30_out, not_31_out,
       not_32_out, not_33_out, not_34_out, not_35_out, not_36_out, not_37_out, not_38_out, not_39_out,
       not_40_out, not_41_out, not_42_out, not_43_out, not_44_out;

  not not_1 (not_1_out, a1);
  and and_1 (and_1_out, not_1_out, not_2_out);
  not not_2 (not_2_out, a3);
  not not_3 (not_3_out, a0);
  and and_2 (and_2_out, not_3_out, a2);
  not not_4 (not_4_out, a0);
  and and_3 (and_3_out, not_4_out, a1, a3);
  and and_4 (and_4_out, a1, a2);
  not not_5 (not_5_out, a1);
  and and_5 (and_5_out, a0, not_5_out, not_6_out);
  not not_6 (not_6_out, a2);
  and and_6 (and_6_out, a0, not_7_out);
  not not_7 (not_7_out, a3);
  not not_8 (not_8_out, a0);
  and and_7 (and_7_out, not_8_out, not_9_out);
  not not_9 (not_9_out, a1);
  not not_10 (not_10_out, a0);
  not not_11 (not_11_out, a2);
  and and_8 (and_8_out, not_10_out, not_11_out, not_12_out);
  not not_12 (not_12_out, a3);
  not not_13 (not_13_out, a1);
  and and_9 (and_9_out, not_13_out, not_14_out);
  not not_14 (not_14_out, a3);
  not not_15 (not_15_out, a0);
  and and_10 (and_10_out, not_15_out, a2, a3);
  not not_16 (not_16_out, a2);
  and and_11 (and_11_out, a0, not_16_out, a3);
  not not_17 (not_17_out, a0);
  and and_12 (and_12_out, not_17_out, not_18_out);
  not not_18 (not_18_out, a2);
  not not_19 (not_19_out, a0);
  and and_13 (and_13_out, not_19_out, a3);
  not not_20 (not_20_out, a2);
  and and_14 (and_14_out, not_20_out, a3);
  not not_21 (not_21_out, a0);
  and and_15 (and_15_out, not_21_out, a1);
  and and_16 (and_16_out, a0, not_22_out);
  not not_22 (not_22_out, a1);
  not not_23 (not_23_out, a0);
  and and_17 (and_17_out, not_23_out, not_24_out, not_25_out);
  not not_24 (not_24_out, a1);
  not not_25 (not_25_out, a3);
  not not_26 (not_26_out, a1);
  and and_18 (and_18_out, not_26_out, a2, a3);
  not not_27 (not_27_out, a2);
  and and_19 (and_19_out, a1, not_27_out, a3);
  and and_20 (and_20_out, a1, a2, not_28_out);
  not not_28 (not_28_out, a3);
  not not_29 (not_29_out, a2);
  and and_21 (and_21_out, a0, not_29_out, not_30_out);
  not not_30 (not_30_out, a3);
  not not_31 (not_31_out, a1);
  and and_22 (and_22_out, not_31_out, not_32_out);
  not not_32 (not_32_out, a3);
  and and_23 (and_23_out, a2, not_33_out);
  not not_33 (not_33_out, a3);
  and and_24 (and_24_out, a0, a2);
  and and_25 (and_25_out, a0, a1);
  not not_34 (not_34_out, a2);
  and and_26 (and_26_out, not_34_out, not_35_out);
  not not_35 (not_35_out, a3);
  not not_36 (not_36_out, a0);
  and and_27 (and_27_out, not_36_out, a1, not_37_out);
  not not_37 (not_37_out, a2);
  and and_28 (and_28_out, a1, not_38_out);
  not not_38 (not_38_out, a3);
  and and_29 (and_29_out, a0, not_39_out);
  not not_39 (not_39_out, a1);
  and and_30 (and_30_out, a0, a2);
  not not_40 (not_40_out, a1);
  and and_31 (and_31_out, not_40_out, a2);
  and and_32 (and_32_out, a2, not_41_out);
  not not_41 (not_41_out, a3);
  not not_42 (not_42_out, a0);
  and and_33 (and_33_out, not_42_out, a1, not_43_out);
  not not_43 (not_43_out, a2);
  and and_34 (and_34_out, a0, not_44_out);
  not not_44 (not_44_out, a1);
  and and_35 (and_35_out, a0, a3);
  or or_1 (b, and_7_out, and_8_out, and_9_out, and_10_out, and_11_out);
  or or_2 (c, and_12_out, and_13_out, and_14_out, and_15_out, and_16_out);
  or or_3 (d, and_17_out, and_18_out, and_19_out, and_20_out, and_21_out);
  or or_4 (e, and_22_out, and_23_out, and_24_out, and_25_out);
  or or_5 (f, and_26_out, and_27_out, and_28_out, and_29_out, and_30_out);
  or or_6 (g, and_31_out, and_32_out, and_33_out, and_34_out, and_35_out);
  or or_7 (a, and_1_out, and_2_out, and_3_out, and_4_out, and_5_out, and_6_out);
endmodule

module _2_DEC_16 (
  input  [7:0] in_1,
  output [6:0] out_2,
  output [6:0] out_3
);

  DECODIFICADOR_16 decodificador_16_1 (
    .a0(in_1[7]), .a1(in_1[6]), .a2(in_1[5]), .a3(in_1[4]), .a(out_2[0]), .b(out_2[1]), .c(out_2[2]),
    .d(out_2[3]), .e(out_2[4]), .f(out_2[5]), .g(out_2[6]));
  DECODIFICADOR_16 decodificador_16_2 (
    .a0(in_1[3]), .a1(in_1[2]), .a2(in_1[1]), .a3(in_1[0]), .a(out_3[0]), .b(out_3[1]), .c(out_3[2]),
    .d(out_3[3]), .e(out_3[4]), .f(out_3[5]), .g(out_3[6]));
endmodule
